# Fritzing sketch binary_leds (saved by Fritzing 0.7.10b)
breadboards: 1

parts:
  Arduino1 = Arduino
  LED1 = LED - 5mm [color="Red (633nm)" package="5 mm [THT]"]
  LED2 = LED - 5mm [color="Red (633nm)" package="5 mm [THT]"]
  LED3 = LED - 5mm [color="Red (633nm)" package="5 mm [THT]"]
  LED4 = LED - 5mm [color="Red (633nm)" package="5 mm [THT]"]
  LED5 = LED - 5mm [color="Red (633nm)" package="5 mm [THT]"]
  LED6 = LED - 5mm [color="Red (633nm)" package="5 mm [THT]"]
  LED7 = LED - 5mm [color="Red (633nm)" package="5 mm [THT]"]
  LED8 = LED - 5mm [color="Red (633nm)" package="5 mm [THT]"]
  R1 = Resistor [tolerance=±5% resistance=100 package=THT]
  R2 = Resistor [tolerance=±5% resistance=100 package=THT]
  R3 = Resistor [tolerance=±5% resistance=100 package=THT]
  R4 = Resistor [tolerance=±5% resistance=100 package=THT]
  R5 = Resistor [tolerance=±5% resistance=100 package=THT]
  R6 = Resistor [tolerance=±5% resistance=100 package=THT]
  R7 = Resistor [tolerance=±5% resistance=100 package=THT]
  R8 = Resistor [tolerance=±5% resistance=100 package=THT]

nets:
  N1: Arduino1.GND, R1.Pin_1, R2.Pin_1, R3.Pin_1, R4.Pin_1, R5.Pin_1, R6.Pin_1, R7.Pin_1, R8.Pin_1
  N2: Arduino1.D11, LED1.anode
  N3: Arduino1.D10, LED2.anode
  N4: Arduino1.D9, LED3.anode
  N5: Arduino1.D8, LED4.anode
  N6: Arduino1.D5, LED5.anode
  N7: Arduino1.D4, LED6.anode
  N8: Arduino1.D3, LED7.anode
  N9: Arduino1.D2, LED8.anode
  N10: LED1.cathode, R1.Pin_0
  N11: LED2.cathode, R2.Pin_0
  N12: LED3.cathode, R3.Pin_0
  N13: LED4.cathode, R4.Pin_0
  N14: LED5.cathode, R5.Pin_0
  N15: LED6.cathode, R6.Pin_0
  N16: LED7.cathode, R7.Pin_0
  N17: LED8.cathode, R8.Pin_0

notes:
  Check the source code for this schematic to see which pins will need an LED on them. Don't forget to add a resistor (100 ohms).
