# Fritzing sketch mpu_650 (saved by Fritzing 0.7.10b)
breadboards: 1

parts:
  Arduino1 = Arduino
  Part4 = Tri-Axis Gyro Breakout - L3G4200D
  LED1 = LED - 5mm [color="Red (633nm)" package="5 mm [THT]"]
  R1 = Resistor [tolerance=±5% resistance=100 package=THT]

nets:
  GND: Arduino1.GND, Part4.GND, LED1.cathode
  N1: Arduino1.D8, R1.Pin_0
  +5V: Arduino1.+5V, Part4.VCC
  N2: Arduino1.A4, Part4.SDA
  N3: Arduino1.A5, Part4.SCL
  N4: LED1.anode, R1.Pin_1

notes:
  Hook a LED into pin 8.
  This isn't the same exact board and chip that is used in the code exampes. It was a "Gy-521," with a "MPU6050."
  GND and VCC and swapped on this one, but as long as SCL goes into A4 and SDA goes into A5 you should be fine.
  Note: the examples use a "GY-521," with a "MPU650," chip.
