# Fritzing sketch pong_controller (saved by Fritzing 0.7.10b)
breadboards: 1

parts:
  Arduino1 = Arduino
  R1 = Rotary Potentiometer (Small) [maximum_resistance=10kΩ]
  R2 = Rotary Potentiometer (Small) [maximum_resistance=10kΩ]

nets:
  N1: Arduino1.+5V, R1.leg1, R2.leg1
  N2: Arduino1.GND, R1.leg2, R2.leg2
  N3: Arduino1.A0, R1.wiper
  N4: Arduino1.A1, R2.wiper

notes:
  These are 10K Potentiometers.
