# Fritzing sketch rgb_led (saved by Fritzing 0.7.10b)

parts:
  Arduino1 = Arduino
  LED1 = RGB LED (com. anode, rbg) [package="5 mm [THT]"]

nets:
  N1: Arduino1.D11, LED1.blue_cathode
  N2: Arduino1.D10, LED1.green_cathode
  N3: Arduino1.D9, LED1.red_cathode
  N4: Arduino1.+5V, LED1.common_anode

notes:
  Note:
  You could also use three separate colored LEDs instead of one (but that's your choice).
  This diagram looks kind of funky. But as long as you have the anode in the 5V section, and the other three pins int their correct holes, you should be fine. Check out the "Schematic View," for a better diagram.
